// Logisim project SelectionSort.circ as structural Verilog: 3 circuits, main circuit main
module main (
  input  done,
  input  in_2,
  input  [7:0] data,
  input  data_av
);

  wire clk_out, not_1_out, rst_out, undriven_3;
  wire [7:0] controlled_buffer_1_out, ram_1_data, undriven, undriven_2;

  Clock clk (.out(clk_out));
  Button rst (.out(rst_out));
  Selection_Sort selection_sort_1 ();  // open: data_in, data, address, data_out
  not not_1 (not_1_out, undriven_3);
  RAM ram_1 (.addr(undriven), .data(ram_1_data), .sel(in_2), .clk(clk_out), .ld(undriven_3));  // open: clr
  assign controlled_buffer_1_out = not_1_out ? undriven_2 : 8'bz;  // Controlled_Buffer controlled_buffer_1

  // Notes on the sheet:
  //   data_in
  //   data_out
endmodule

module Selection_Sort (
  input  [7:0] data_in,
  input  [7:0] address,
  input  [7:0] data,
  input  [7:0] data_out
);
endmodule

module DataPath (
  input  wrI,
  input  selAddr,
  input  [7:0] data_in,
  input  wrMin,
  input  sel1min,
  input  sel0min,
  input  selSum0i,
  input  wrI_2,
  input  wrStartAddr,
  input  selSum1i,
  input  selInc,
  input  wrSize,
  input  selComp,
  input  wrI_3,
  input  [7:0] data,
  input  wrOrder,
  input  clock,
  input  reset,
  output out_19,
  output [7:0] address,
  output lt_size,
  output [7:0] data_out
);

  wire comparator_1_gt, comparator_1_lt;
  wire [6:0] subtractor_1_out;
  wire [7:0] adder_1_out, and_1_out, multiplexer_1_out, multiplexer_2_out, multiplexer_3_out,
       multiplexer_4_out, multiplexer_6_out, reg_aux_q, reg_i_q, reg_J_q, reg_min_q, reg_order_q, reg_size_q,
       reg_startAddr_q, undriven;

  // Probe on data_in
  // Probe on data
  Register reg_startAddr (.D(data), .en(wrStartAddr), .Q(reg_startAddr_q), .clk(clock), .clr(reset));
  Register reg_size (.D(data), .en(wrSize), .Q(reg_size_q), .clk(clock), .clr(reset));
  Register reg_order (.D(data), .en(wrOrder), .Q(reg_order_q), .clk(clock), .clr(reset));
  Multiplexer #(.width(8), .disabled(0), .enable("false")) multiplexer_1 (
    .in0(adder_1_out), .in1(undriven), .out(multiplexer_1_out), .sel(selSum0i));
  assign and_1_out = reg_order_q & 8'h1;  // AND_Gate and_1, 8 bits wide
  Multiplexer #(.width(8), .disabled(0), .enable("false")) multiplexer_2 (
    .in0(multiplexer_1_out), .in1(reg_startAddr_q), .out(multiplexer_2_out), .sel(selSum1i));
  Register reg_i (.D(multiplexer_2_out), .en(wrI_2), .Q(reg_i_q), .clk(clock), .clr(reset));
  Register reg_J (.D(adder_1_out), .en(wrI_3), .Q(reg_J_q), .clk(clock), .clr(reset));
  Register reg_aux (.D(data_in), .en(wrI), .Q(reg_aux_q), .clk(clock), .clr(reset));
  Multiplexer #(.select(2), .width(8), .disabled(0), .enable("false")) multiplexer_3 (
    .in0(reg_i_q), .in1(data_in), .in2(reg_J_q), .out(multiplexer_3_out), .sel({sel1min, sel0min}));  // open: in3
  Multiplexer #(.width(8), .disabled(0), .enable("false")) multiplexer_4 (
    .in0(reg_i_q), .in1(reg_J_q), .out(multiplexer_4_out), .sel(selInc));
  Register reg_min (.D(multiplexer_3_out), .en(wrMin), .Q(reg_min_q), .clk(clock), .clr(reset));
  Adder adder_1 (.a(multiplexer_4_out), .b(8'h1), .out(adder_1_out));  // open: cin, cout
  Comparator comparator_1 (.a(reg_aux_q), .b(data_in), .gt(comparator_1_gt), .lt(comparator_1_lt));  // open: eq
  Multiplexer #(.enable("false")) multiplexer_5 (
    .in0(comparator_1_gt), .in1(comparator_1_lt), .out(out_19), .sel(and_1_out[0]));
  // Probe on multiplexer_6_out
  Multiplexer #(.width(8), .disabled(0), .enable("false")) multiplexer_6 (
    .in0(adder_1_out), .in1(reg_J_q), .out(multiplexer_6_out), .sel(selComp));
  Multiplexer #(.width(8), .enable("false")) multiplexer_7 (
    .in0(reg_min_q), .in1(reg_J_q), .out(address), .sel(selAddr));
  Subtractor subtractor_1 (
    .a(multiplexer_6_out), .b(reg_size_q), .out({lt_size, subtractor_1_out}));  // open: bin, bout

  // Other names for the same wires on the sheet: clk = clock; rst = reset

  // Notes on the sheet:
  //   i++
  //   i ^ min
  //   ld address
  //   i++
  //   j++
  //   i + 1 < size
  //   j < size
endmodule
